# Fritzing sketch Sketch for tex (saved by Fritzing 0.9.2b)

parts:
  Part1 = Arduino Uno (Rev3)
  NEOPIXEL1 = Neopixel Strip -- Black (60/m)
  NEOPIXEL2 = Neopixel Strip -- Black (60/m)
  NEOPIXEL3 = Neopixel Strip -- Black (60/m)
  NEOPIXEL4 = Neopixel Strip -- Black (60/m)
  NEOPIXEL5 = Neopixel Strip -- Black (60/m)
  Part2 = HX711 Weighing Sensor Module
  Raspberry_Pi1 = Raspberry Pi 2  # not connected

nets:
  N1: Part1.A0, Part2.CK/TX
  N2: Part1.A1, Part2.DO/RX
  N3: Part1.D3_PWM, NEOPIXEL4.+5V
  N4: Part1.D4, NEOPIXEL3.+5V
  N5: Part1.D5_PWM, NEOPIXEL2.+5V
  N6: Part1.D6_PWM, NEOPIXEL5.+5V
  N7: Part1.D7, NEOPIXEL1.+5V
  GND: Part1.GND, NEOPIXEL1.GND, NEOPIXEL2.GND, NEOPIXEL3.GND, NEOPIXEL4.GND, NEOPIXEL5.GND, Part2.GND
  VIN: Part1.VIN, NEOPIXEL1.DI, NEOPIXEL2.DI, NEOPIXEL3.DI, NEOPIXEL4.DI, NEOPIXEL5.DI, Part2.VCC

notes:
  WiFi
  Scale
  Floor
  Glasses
  Ice & Shaker
  Shelves
  Weighting module

custom parts:
  Neopixel Strip -- Black (60/m): Neopixel Strip, Black, 60 pixels per meter.
